// Digital circuit part_c.dig as structural Verilog
module part_c (
  input  in_0,
  input  in_1,
  input  in_2,
  output out_0
);

  wire fgnfet_1_s, fgnfet_3_s, fgnfet_7_d, fgpfet_1_d, fgpfet_2_d, fgpfet_5_d, fgpfet_6_d, pfet_1_d;

  FGPFET fgpfet_1 (.G(in_0), .S(1'b1), .D(fgpfet_1_d));
  FGNFET fgnfet_1 (.G(in_0), .D(fgpfet_1_d), .S(fgnfet_1_s));
  FGNFET fgnfet_2 (.G(in_1), .D(fgnfet_1_s), .S(1'b0));
  FGPFET fgpfet_2 (.G(in_2), .S(1'b1), .D(fgpfet_2_d));
  FGNFET fgnfet_3 (.G(in_2), .D(fgpfet_2_d), .S(fgnfet_3_s));
  FGNFET fgnfet_4 (.G(in_0), .D(fgnfet_3_s), .S(1'b0));
  FGPFET fgpfet_3 (.G(in_1), .S(1'b1), .D(fgpfet_1_d));
  FGPFET fgpfet_4 (.G(in_0), .S(1'b1), .D(fgpfet_2_d));
  FGPFET fgpfet_5 (.G(fgpfet_1_d), .S(1'b1), .D(fgpfet_5_d));
  FGNFET fgnfet_5 (.G(fgpfet_1_d), .D(fgpfet_5_d), .S(1'b0));
  FGPFET fgpfet_6 (.G(fgpfet_2_d), .S(1'b1), .D(fgpfet_6_d));
  FGNFET fgnfet_6 (.G(fgpfet_2_d), .D(fgpfet_6_d), .S(1'b0));
  PFET pfet_1 (.G(fgpfet_5_d), .S(1'b1), .D(pfet_1_d));
  FGNFET fgnfet_7 (.G(fgpfet_6_d), .D(fgnfet_7_d), .S(1'b0));
  FGNFET fgnfet_8 (.G(fgpfet_6_d), .D(fgnfet_7_d), .S(1'b0));
  PFET pfet_2 (.G(fgpfet_6_d), .S(pfet_1_d), .D(fgnfet_7_d));
  FGNFET fgnfet_9 (.G(fgpfet_5_d), .D(fgnfet_7_d), .S(1'b0));
  FGPFET fgpfet_7 (.G(fgnfet_7_d), .S(1'b1), .D(out_0));
  FGNFET fgnfet_10 (.G(fgnfet_7_d), .D(out_0), .S(1'b0));
endmodule

/* Test case part_c_test:
in_0 in_1 in_2 out_0
0    0    0    0
0    0    1    0
0    1    0    0
0    1    1    0
1    0    0    0
1    0    1    1
1    1    0    1
1    1    1    1
*/
